// Logisim project Milestone2COTarekZeyad.circ as structural Verilog: 2 circuits, main circuit main
module main (
  output out_1
);

  wire and_7_out, and_8_out, and_9_out, and_10_out, and_11_out, and_12_out, and_13_out, and_14_out,
       and_15_out, and_16_out, and_18_out, and_19_out, and_20_out, and_21_out, and_23_out, and_30_out, B0,
       B1, B2, B3, B4, B5, B6, B7, B8, B9, B10, B11, Check_AC, CLA_SC, Clock, D0, D1, D2, D3, D4, D5, D6, D7,
       d_ff_1_q, I, II, INC_PC, INC_SC, Load_PC, LoadAC, LoadAR, LoadDR, Mem_Enab, Mem_write, not_1_out,
       not_5_out, or_9_out, or_10_out, T0, T1, T2, T3, T3IdD7B5, T4, T4_t, T4D0, T4D1, T4D2, T4D3, T4D5, T5,
       T5D0, T5D1, T5D2, T5D5, T6, T6D5, T7, T8, T9, T10, T11, T12, T13, T14, T15, X0, X1, X4, Y3, Y7;
  wire [2:0] priority_encoder_1_out, priority_encoder_2_out;
  wire [3:0] SC_q;
  wire [6:0] AR_q, bit_extender_1_out, bit_extender_2_out, PC_q;
  wire [14:12] IR_q;
  wire [15:0] AC, ALU_ac_output, bit_extender_3_out, bit_extender_4_out, bit_extender_5_out, DR_q,
       multiplexer_1_out, ram_1_data, TR_q;

  or or_1 (X0, T4D1, T4D2, T4D0, T1, T4D5);
  and and_1 (T5D5, T5, D5);
  Bit_Extender #(.in_width(16), .out_width(7)) bit_extender_1 (.in(multiplexer_1_out), .out(bit_extender_1_out));
  Register #(.width(16)) IR (
    .D(multiplexer_1_out), .en(T1), .Q({I, IR_q, B11, B10, B9, B8, B7, B6, B5, B4, B3, B2, B1, B0}),
    .clk(Clock));  // open: clr
  and and_2 (Load_PC, D4, T4);
  and and_3 (T4D2, T4, D2);
  and and_4 (T4D1, T4, D1);
  and and_5 (T4D5, T4, D5);
  and and_6 (T4D0, T4, D0);
  not not_1 (not_1_out, I);
  Bit_Extender #(.in_width(16), .out_width(7)) bit_extender_2 (.in(multiplexer_1_out), .out(bit_extender_2_out));
  or or_2 (LoadAR, T0, T2);
  and and_7 (and_7_out, T4_t, D1);
  and and_8 (and_8_out, T4_t, D2);
  and and_9 (and_9_out, B5, D7, T3, not_1_out);
  and and_10 (and_10_out, not_1_out, T3, D7, B2, Check_AC);
  or or_3 (Mem_Enab, T1, T4D2, T4D1, T4D5, T4D0);
  Register #(.width(7)) AR (.D(bit_extender_1_out), .en(LoadAR), .Q(AR_q), .clk(Clock));  // open: clr
  Register #(.width(16)) TR (.D(multiplexer_1_out), .en(1'b0), .Q(TR_q), .clk(Clock));  // open: clr
  Register #(.width(16)) DR (.D(multiplexer_1_out), .en(LoadDR), .Q(DR_q), .clk(Clock));  // open: clr
  Register #(.width(16)) u_AC (.D(ALU_ac_output), .en(LoadAC), .Q(AC), .clk(Clock));  // open: clr
  Counter #(.width(7), .max('h7f)) PC (
    .load(Load_PC), .D(bit_extender_2_out), .count(INC_PC), .Q(PC_q), .clk(Clock));  // open: carry, clr
  Decoder #(.select(3), .enable("false")) decoder_1 (
    .out0(D0), .out1(D1), .out2(D2), .out3(D3), .out4(D4), .out5(D5), .out6(D6), .out7(D7), .sel(IR_q));
  and and_11 (and_11_out, T4_t, D5);
  and and_12 (and_12_out, D5, T5);
  and and_13 (and_13_out, D3, T4);
  and and_14 (and_14_out, T4, D5);
  or or_4 (X4, T5D5, T4D3, T3IdD7B5);
  RAM #(.addrWidth(7), .dataWidth(16), .bus("separate")) ram_1 (
    .addr(AR_q), .din(multiplexer_1_out), .data(ram_1_data), .str(Mem_write), .clk(Clock), .ld(Mem_Enab));  // open: sel, clr
  Counter #(.width(4), .max('hf)) SC (.count(INC_SC), .Q(SC_q), .clk(Clock), .clr(d_ff_1_q));  // open: load, D, carry
  D_Flip_Flop d_ff_1 (.clk(Clock), .D(CLA_SC), .Q(d_ff_1_q));  // open: Qn, preset, en, reset
  or or_5 (INC_PC, T1, and_10_out);
  or or_6 (Mem_write, and_13_out, and_14_out);
  assign bit_extender_3_out = {{9{1'b0}}, AR_q};  // Bit_Extender bit_extender_3
  ALU ALU (.A(DR_q), .B(AC), .in_3(priority_encoder_1_out), .E(out_1), .AC_Output(ALU_ac_output));
  assign bit_extender_4_out = {{9{1'b0}}, PC_q};  // Bit_Extender bit_extender_4
  Decoder #(.select(4), .enable("false")) decoder_2 (
    .out0(T0), .out1(T1), .out2(T2), .out3(T3), .out4(T4), .out5(T5), .out6(T6), .out7(T7), .out8(T8),
    .out9(T9), .out10(T10), .out11(T11), .out12(T12), .out13(T13), .out14(T14), .out15(T15), .sel(SC_q));
  and and_15 (and_15_out, T4_t, D0);
  not not_2 (II, I);
  or or_7 (Y3, T5D5, T5D2);
  or or_8 (LoadDR, and_15_out, and_7_out, and_8_out, and_11_out, and_12_out, and_9_out);
  and and_16 (and_16_out, T5, D0);
  and and_17 (X1, T4, D4);
  and and_18 (and_18_out, T5, D2);
  and and_19 (and_19_out, T5, D1);
  and and_20 (and_20_out, T6, D5);
  and and_21 (and_21_out, B5, T4, II, D7);
  and and_22 (T4D3, T4, D3);
  and and_23 (and_23_out, T3, II, B2, D7);
  Clock clock_1 (.out(Clock));
  and and_24 (T3IdD7B5, B5, II, T3, D7);
  not not_3 (INC_SC, CLA_SC);
  or or_9 (or_9_out, T5D5, T5D2);
  or or_10 (or_10_out, AC[0], AC[1], AC[2], AC[3], AC[4], AC[5], AC[6], AC[7], AC[8], AC[9], AC[10], AC[11], AC[12], AC[13], AC[14], AC[15]);
  not not_4 (Check_AC, or_10_out);
  or or_11 (CLA_SC, and_16_out, X1, and_18_out, and_19_out, and_20_out, and_21_out, T4D3, and_23_out);
  Multiplexer #(.select(3), .width(16), .enable("false")) multiplexer_1 (
    .in0(ram_1_data), .in1(bit_extender_3_out), .in2(TR_q), .in3(DR_q), .in4(AC), .in5(bit_extender_4_out),
    .in6(bit_extender_5_out), .out(multiplexer_1_out), .sel(priority_encoder_2_out));  // open: in7
  assign bit_extender_5_out = {{4{1'b0}}, {B11, B10, B9, B8, B7, B6, B5, B4, B3, B2, B1, B0}};  // Bit_Extender bit_extender_5
  and and_25 (T5D0, D0, T5);
  not not_5 (not_5_out, I);
  and and_26 (Y7, T4, II, D7, B5);
  and and_27 (T5D1, T5, D1);
  and and_28 (T5D5, T5, D5);
  and and_29 (T6D5, D5, T6);
  and and_30 (and_30_out, T4, D7, B5, not_5_out);
  Priority_Encoder priority_encoder_1 (
    .in1(T5D1), .in2(T6D5), .in3(or_9_out), .in4(T5D0), .in7(Y7), .out(priority_encoder_1_out), .en_in(1'b1));  // open: in0, in5, in6, gs, en_out
  and and_31 (T5D2, T5, D2);
  Priority_Encoder priority_encoder_2 (
    .in0(X0), .in1(X1), .in4(X4), .in5(T0), .in6(T2), .out(priority_encoder_2_out), .en_in(1'b1));  // open: in2, in3, in7, gs, en_out
  or or_12 (LoadAC, T5D0, T5D2, T5D1, T5D5, T6D5, and_30_out);

  // Other names for the same wires on the sheet: IRR[11:0] = {B11, B10, B9, B8, B7, B6, B5, B4, B3, B2, B1, B0}
endmodule

module ALU (
  input  [15:0] A,
  input  [15:0] B,
  input  [2:0] in_3,
  output E,
  output [15:0] AC_Output
);

  wire adder_1_cout, adder_2_cout, subtractor_1_bout;
  wire [15:0] adder_1_out, adder_2_out, and_1_out, or_1_out, subtractor_1_out, xor_1_out;

  Adder #(.width(16)) adder_1 (.a(A), .b(B), .out(adder_1_out), .cin(1'b0), .cout(adder_1_cout));
  Subtractor #(.width(16)) subtractor_1 (.a(A), .b(B), .out(subtractor_1_out), .bin(1'b0), .bout(subtractor_1_bout));
  assign and_1_out = A & B;  // AND_Gate and_1, 16 bits wide
  assign or_1_out = A | B;  // OR_Gate or_1, 16 bits wide
  assign xor_1_out = A ^ B;  // XOR_Gate xor_1, 16 bits wide
  Adder #(.width(16)) adder_2 (.a(A), .b({16{1'b0}}), .out(adder_2_out), .cin(1'b1), .cout(adder_2_cout));
  or or_2 (E, adder_1_cout, subtractor_1_bout, adder_2_cout);
  Multiplexer #(.select(3), .width(16)) multiplexer_1 (
    .in1(adder_1_out), .in2(subtractor_1_out), .in3(A), .in4(and_1_out), .in5(or_1_out), .in6(xor_1_out),
    .in7(adder_2_out), .out(AC_Output), .sel(in_3));  // open: in0, en
endmodule
